// Logisim project 4BitParity1-1.circ as structural Verilog: 8 circuits, main circuit main
module main (
  input  Halt_Enable
);

  wire and_2_out, CLK, Correct, Done_Testing, Halt, Input, not_1_out, not_2_out, not_3_out, Solution,
       YourAnswer;
  wire [6:0] counter_1_q, TestNumber;

  not not_1 (not_1_out, Correct);
  Clock clock_1 (.out(CLK));
  and and_1 (Halt, Halt_Enable, not_1_out);
  Inputs inputs_1 (.Halt(Halt), .CLK(CLK), .Input(Input), .TestNumber(TestNumber), .Done_Testing(Done_Testing));
  _4BitEvenParity u_4bitevenparity_1 (.Input(Input), .CLK(CLK), .Is_Even(YourAnswer));
  // Probe on Input
  // Probe on YourAnswer
  // Probe on Solution
  // Probe on Correct
  not not_2 (not_2_out, Halt);
  and and_2 (and_2_out, Correct, not_2_out, not_3_out);
  not not_3 (not_3_out, Done_Testing);
  Checker checker_1 (.Your_Answer(YourAnswer), .TestNumber(TestNumber), .Correct(Correct), .Solution(Solution));
  Counter #(.width(7), .max('h41), .ongoal("stay")) counter_1 (
    .count(and_2_out), .Q(counter_1_q), .clk(CLK));  // open: load, D, carry, clr
  // Probe on counter_1_q

  // Notes on the sheet:
  //   dongzhu pan
  //   shikun huang
  //   Max 65
endmodule

module _4BitEvenParity (
  input  Input,
  input  CLK,
  output Is_Even
);

  wire a, b, c, s1_1_out1, s2_1_out2, s3_1_out3, s4_1_out4;

  s1 s1_1 (.x1(a), .x2(b), .x3(c), .in(Input), .out1(s1_1_out1));
  s2 s2_1 (.x1(a), .x2(b), .x3(c), .in(Input), .out2(s2_1_out2));
  s3 s3_1 (.x1(a), .x2(b), .x3(c), .in(Input), .out3(s3_1_out3));
  s4 s4_1 (.x1(a), .x2(b), .x3(c), .in(Input), .out4(s4_1_out4));
  D_Flip_Flop d_ff_1 (.clk(CLK), .D(s1_1_out1), .Q(a));  // open: Qn, preset, en, reset
  D_Flip_Flop d_ff_2 (.clk(CLK), .D(s2_1_out2), .Q(b));  // open: Qn, preset, en, reset
  D_Flip_Flop d_ff_3 (.clk(CLK), .D(s3_1_out3), .Q(c));  // open: Qn, preset, en, reset
  D_Flip_Flop d_ff_4 (.clk(CLK), .D(s4_1_out4), .Q(Is_Even));  // open: Qn, preset, en, reset

  // Other names for the same wires on the sheet: d = Is_Even; in = Input
endmodule

module Inputs (
  input  Halt,
  input  CLK,
  output Input,
  output [6:0] TestNumber,
  output Done_Testing
);

  wire not_1_out;

  not not_1 (not_1_out, Halt);
  Counter #(.width(7), .max('h41), .ongoal("stay")) counter_1 (
    .count(not_1_out), .Q(TestNumber), .carry(Done_Testing), .clk(CLK));  // open: load, D, clr
  ROM #(.addrWidth(7), .dataWidth(1)) rom_1 (.addr(TestNumber), .data(Input));  // open: sel

  // Notes on the sheet:
  //   contents of rom_1 (hex, n*v repeats v):
  //   7*0 1 0 0 1 0 0 0 1 1 0 1 0 0 0 1 0 1 0 1 1 0 0 4*1 0 0 0 1 0 0 1 1 0 1 0 1 0 4*1 0 0 1 1 0 4*1 0
  //   4*1
endmodule

module Checker (
  input  Your_Answer,
  input  [6:0] TestNumber,
  output Correct,
  output Solution
);

  ROM #(.addrWidth(7), .dataWidth(1)) rom_1 (.addr(TestNumber), .data(Solution));  // open: sel
  Comparator #(.width(1)) comparator_1 (.a(Solution), .b(Your_Answer), .eq(Correct));  // open: gt, lt

  // Notes on the sheet:
  //   contents of rom_1 (hex, n*v repeats v):
  //   4*0 1 11*0 1 7*0 1 0 0 0 1 11*0 1 0 0 0 1 7*0 1 11*0 1
endmodule

module s1 (
  input  x1,
  input  x2,
  input  x3,
  input  in,
  output out1
);

  wire and_1_out, and_2_out, and_3_out, and_4_out, not_1_out, not_2_out, not_3_out, not_4_out, not_5_out;

  not not_1 (not_1_out, x1);
  and and_1 (and_1_out, not_1_out, x3, not_2_out);
  not not_2 (not_2_out, in);
  not not_3 (not_3_out, x1);
  and and_2 (and_2_out, not_3_out, x2, in);
  not not_4 (not_4_out, x3);
  and and_3 (and_3_out, x1, not_4_out, in);
  and and_4 (and_4_out, x1, x2, not_5_out);
  not not_5 (not_5_out, in);
  or or_1 (out1, and_1_out, and_2_out, and_3_out, and_4_out);
endmodule

module s2 (
  input  x1,
  input  x2,
  input  x3,
  input  in,
  output out2
);

  wire and_1_out, and_2_out, and_3_out, and_4_out, not_1_out, not_2_out, not_3_out, not_4_out, not_5_out,
       not_6_out;

  not not_1 (not_1_out, x1);
  and and_1 (and_1_out, not_1_out, in);
  not not_2 (not_2_out, x1);
  not not_3 (not_3_out, x2);
  and and_2 (and_2_out, not_2_out, not_3_out, x3);
  not not_4 (not_4_out, x2);
  and and_3 (and_3_out, not_4_out, x3, in);
  and and_4 (and_4_out, x2, not_5_out, not_6_out);
  not not_5 (not_5_out, x3);
  not not_6 (not_6_out, in);
  or or_1 (out2, and_1_out, and_2_out, and_3_out, and_4_out);
endmodule

module s3 (
  input  x1,
  input  x2,
  input  x3,
  input  in,
  output out3
);

  wire and_1_out, and_2_out, and_3_out, and_4_out, and_5_out, not_1_out, not_2_out, not_3_out, not_4_out,
       not_5_out, not_6_out, not_7_out, not_8_out, not_9_out;

  not not_1 (not_1_out, x1);
  not not_2 (not_2_out, x3);
  not not_3 (not_3_out, in);
  not not_4 (not_4_out, x1);
  not not_5 (not_5_out, x3);
  not not_6 (not_6_out, in);
  not not_7 (not_7_out, x2);
  not not_8 (not_8_out, x3);
  not not_9 (not_9_out, in);
  and and_1 (and_1_out, not_1_out, not_2_out, not_3_out);
  and and_2 (and_2_out, not_4_out, x3, in);
  and and_3 (and_3_out, x2, not_5_out, not_6_out);
  and and_4 (and_4_out, x1, not_7_out, not_8_out, in);
  and and_5 (and_5_out, x1, x3, not_9_out);
  or or_1 (out3, and_1_out, and_2_out, and_3_out, and_4_out, and_5_out);
endmodule

module s4 (
  input  x1,
  input  x2,
  input  x3,
  input  in,
  output out4
);

  wire and_1_out, and_2_out, not_1_out, not_2_out, not_3_out;

  not not_1 (not_1_out, x2);
  not not_2 (not_2_out, x3);
  not not_3 (not_3_out, in);
  and and_1 (and_1_out, x1, not_1_out, not_2_out, in);
  or or_1 (out4, and_1_out, and_2_out);
  and and_2 (and_2_out, x1, x2, x3, not_3_out);
endmodule
