// Logisim project finishedgrey.circ as structural Verilog: 4 circuits, main circuit main
module main (
);

  wire and_1_out, Checker_correct, clock_1_out, clock_2_out, clock_3_out, Not_Done, x0, x1, x2;
  wire [2:0] part2_1_y0;
  wire [3:0] counter_1_q;

  Inputs Inputs (.Clock(clock_1_out), .Not_Done(Not_Done), .x2(x2), .x1(x1), .x0(x0));
  Clock clock_1 (.out(clock_1_out));
  part2 part2_1 (.x2(x2), .x1(x1), .x0(x0), .y2(part2_1_y0[2]), .y1(part2_1_y0[1]), .y0(part2_1_y0[0]));
  Checker Checker (.x2(x2), .x1(x1), .x0(x0), .YourSolution(part2_1_y0), .Correct(Checker_correct));
  Shift_Register Correct (
    .shift(Not_Done), .in(Checker_correct), .clk(clock_2_out));  // open: out, load, clr, d0, q0, d1, q1, d2, q2, d3, q3, d4, q4, d5, q5, d6, q6, d7, q7
  Clock clock_2 (.out(clock_2_out));
  and and_1 (and_1_out, Checker_correct, Not_Done);
  Counter #(.width(4), .max('hf), .ongoal("stay")) counter_1 (
    .count(and_1_out), .Q(counter_1_q), .clk(clock_3_out));  // open: load, D, carry, clr
  Clock clock_3 (.out(clock_3_out));
  // Probe on counter_1_q

  // Notes on the sheet:
  //   ECS 154 A
  //   DAVID HADDAD         STUDENT ID  913868711
  //   SHIKUN HUANG         STUDENT ID  915810013
  //   Put Your Answer In Here
endmodule

module part2 (
  input  x2,
  input  x1,
  input  x0,
  output y2,
  output y1,
  output y0
);

  xor xor_1 (y1, x2, x1);
  xor xor_2 (y0, x1, x0);

  assign y2 = x2;
endmodule

module Inputs (
  input  Clock,
  output Not_Done,
  output x2,
  output x1,
  output x0
);

  wire [3:3] counter_1_q;

  Counter #(.width(4), .max('h8), .ongoal("stay")) counter_1 (
    .count(1'b1), .Q({counter_1_q[3], x2, x1, x0}), .clk(Clock));  // open: load, D, carry, clr
  not not_1 (Not_Done, counter_1_q[3]);
endmodule

module Checker (
  input  x2,
  input  x1,
  input  x0,
  input  [2:0] YourSolution,
  output Correct
);

  wire [2:0] rom_1_data;

  ROM #(.addrWidth(3), .dataWidth(3)) rom_1 (.addr({x2, x1, x0}), .data(rom_1_data));  // open: sel
  Comparator #(.width(3)) comparator_1 (.a(rom_1_data), .b(YourSolution), .eq(Correct));  // open: gt, lt

  // Notes on the sheet:
  //   contents of rom_1 (hex, n*v repeats v):
  //   0 1 3 2 6 7 5 4
endmodule
